# Fritzing sketch design (saved by Fritzing 0.6.3b)
breadboards: 1

parts:
  Arduino1 = Arduino
  S1 = Pushbutton [package=THT]
  S2 = Pushbutton [package=THT]
  R1 = Resistor [tolerance=±5% resistance=1k package=THT]
  R2 = Resistor [tolerance=±5% resistance=1k package=THT]
  R3 = Resistor [tolerance=±5% resistance=1k package=THT]
  R4 = Photocell (LDR) [package=THT]

nets:
  N1: Arduino1.D7, S2.leg0, R1.Pin_1
  N2: Arduino1.D6, S1.leg0, R2.Pin_1
  N3: Arduino1.+5V, S1.leg1, S2.leg1, R4.pin_0
  N4: Arduino1.GND, R1.Pin_0, R2.Pin_0, R3.Pin_0
  N5: Arduino1.A0, R3.Pin_1, R4.pin_1
